# Fritzing sketch i2c_lamp_simulator (saved by Fritzing 0.9.4)
breadboards: 1

parts:
  Composant1 = Arduino Uno (Rev3)
  Power_plug1 = Power plug
  Composant2 = Arduino Uno (Rev3)
  S1 = Pushbutton [package="[THT]"]
  R1 = Resistor [tolerance=±5% resistance=3k package=THT]
  R2 = Resistor [tolerance=±5% resistance=3k package=THT]
  R3 = Resistor [tolerance=±5% resistance=3k package=THT]

nets:
  N1: Composant1.A4/SDA, Composant2.A4/SDA, R2.Pin_1
  N2: Composant1.A5/SCL, Composant2.A5/SCL, R1.Pin_1
  N3: Composant1.D12/MISO, S1.Pin_3, S1.Pin_4, R3.Pin_1
  GND: Composant1.GND, Power_plug1.GND, Composant2.GND, S1.Pin_1, S1.Pin_2
  5V: Composant1.5V, Power_plug1.VCC, Composant2.5V, R1.Pin_0, R2.Pin_0, R3.Pin_0
